# Fritzing sketch door lock_unlock (Labelled) (saved by Fritzing 0.9.3b)
breadboards: 1

parts:
  ARDUINO_UNO = Arduino Uno (Rev3)
  L293D_MOTOR_DRIVER = L293D [package=THT]
  DC_MOTOR = DC Motor
  BLUETOOTH_MODULE_(HC-05) = Bluetooth HC-05 Macho
  BATTERY_HOLDER = Battery Holders [package=battery_20mm_pth_compact]

nets:
  N1: ARDUINO_UNO.D10_PWM/SS, L293D_MOTOR_DRIVER.In_3
  N2: ARDUINO_UNO.D11_PWM/MOSI, L293D_MOTOR_DRIVER.In_4
  N3: ARDUINO_UNO.D0/RX, BLUETOOTH_MODULE_(HC-05).TXD
  N4: ARDUINO_UNO.D1/TX, BLUETOOTH_MODULE_(HC-05).RXD
  N5: ARDUINO_UNO.5V, L293D_MOTOR_DRIVER.Enable_2, L293D_MOTOR_DRIVER.+V
  GND: ARDUINO_UNO.GND, L293D_MOTOR_DRIVER.0V, BLUETOOTH_MODULE_(HC-05).GND, BATTERY_HOLDER.-
  VIN: ARDUINO_UNO.VIN, L293D_MOTOR_DRIVER.+Vmotor, BLUETOOTH_MODULE_(HC-05).VCC, BATTERY_HOLDER.+
  N6: L293D_MOTOR_DRIVER.Out_3_(_Controlled_by_Enable_2_), DC_MOTOR.pin_2
  N7: L293D_MOTOR_DRIVER.Out_4_(_Controlled_by_Enable_2_), DC_MOTOR.pin_1
