# Fritzing sketch home_automation_up(labelled) (saved by Fritzing 0.9.3b)
breadboards: 2

parts:
  ESP_Module = NodeMCU V1.0
  Battery = Battery block 9V
  Voltage_Reguator = Voltage Regulator - 5V [package="TO220 [THT]"]
  Relay_Module = 4-Channel 5v Relay Shield [package=relay-4ch5v10a]
  LED1 = smd LED [color="Red (633nm)" package="0805 [SMD]"]
  LED2 = smd LED [color="Red (633nm)" package="0805 [SMD]"]
  LED3 = smd LED [color="Red (633nm)" package="0805 [SMD]"]  # not connected
  LED4 = smd LED [color="Red (633nm)" package="0805 [SMD]"]

nets:
  N1: ESP_Module.D0, Relay_Module.IN1
  N2: ESP_Module.D1, Relay_Module.IN2
  N3: ESP_Module.D2, Relay_Module.IN3
  N4: ESP_Module.D3, Relay_Module.IN4
  GND: ESP_Module.GND, Battery.-, Voltage_Reguator.GND, Relay_Module.GND, LED1.cathode, LED2.cathode, LED4.cathode
  N5: ESP_Module.Vin, Voltage_Reguator.output_voltage
  N6: Battery.+, Voltage_Reguator.input_voltage, Relay_Module.VCC, Relay_Module.K1-In, Relay_Module.K2-In, Relay_Module.K3-In, Relay_Module.K4-In
  N7: Relay_Module.K1-On, LED1.anode
  N8: Relay_Module.K2-On, LED4.anode
  N9: Relay_Module.K3-On, LED2.anode

custom parts:
  NodeMCU V1.0: ESP8266 based NodeMCU
  4-Channel 5v Relay Shield: 4 Channel 5v Relay Shield w. 2x SPD-06VDC-SD-C
