# Fritzing sketch home_automation_up (saved by Fritzing 0.9.3b)
breadboards: 2

parts:
  U1 = NodeMCU V1.0
  VCC1 = Battery block 9V
  U2 = Voltage Regulator - 5V [package="TO220 [THT]"]
  U3 = 4-Channel 5v Relay Shield [package=relay-4ch5v10a]
  LED1 = smd LED [color="Red (633nm)" package="0805 [SMD]"]
  LED2 = smd LED [color="Red (633nm)" package="0805 [SMD]"]
  LED3 = smd LED [color="Red (633nm)" package="0805 [SMD]"]  # not connected
  LED4 = smd LED [color="Red (633nm)" package="0805 [SMD]"]

nets:
  N1: U1.D0, U3.IN1
  N2: U1.D1, U3.IN2
  N3: U1.D2, U3.IN3
  N4: U1.D3, U3.IN4
  GND: U1.GND, VCC1.-, U2.GND, U3.GND, LED1.cathode, LED2.cathode, LED4.cathode
  N5: U1.Vin, U2.output_voltage
  N6: VCC1.+, U2.input_voltage, U3.VCC, U3.K1-In, U3.K2-In, U3.K3-In, U3.K4-In
  N7: U3.K1-On, LED1.anode
  N8: U3.K2-On, LED4.anode
  N9: U3.K3-On, LED2.anode

custom parts:
  NodeMCU V1.0: ESP8266 based NodeMCU
  4-Channel 5v Relay Shield: 4 Channel 5v Relay Shield w. 2x SPD-06VDC-SD-C
