# Fritzing sketch waterlevel (Labelled) (saved by Fritzing 0.9.3b)
circuit board: 8.46667cm x 5.64444cm
breadboards: 1

parts:
  NODE_MCU = NodeMCU V1.0
  BUZZER = Piezo Speaker
  BATTERY_HOLDER = Battery Holders [package=battcon_12mm_pth]
  RELAY = RELAY [package=relay-t9a]
  NPN_TRANSISTOR = NPN-Transistor [package="SOT-23 [SMD]"]
  DC_MOTOR = DC Motor
  ULTRASONIC_SENSOR = HC-SR04 Ultrasonic Distance Sensor
  RESISTOR = Resistor [tolerance=±5% resistance=220 package="0402 [SMD]"]

nets:
  N1: NODE_MCU.D2, ULTRASONIC_SENSOR.TRIG
  GND: NODE_MCU.D4, NODE_MCU.GND, BUZZER.pin1, BATTERY_HOLDER.-, RELAY.COIL2, DC_MOTOR.pin_1, ULTRASONIC_SENSOR.ECHO, ULTRASONIC_SENSOR.GND
  N2: NODE_MCU.D7, BUZZER.pin2
  N3: NODE_MCU.D8, RESISTOR.Pin_1
  VIN: NODE_MCU.Vin, BATTERY_HOLDER.+, RELAY.MAIN, NPN_TRANSISTOR.2, ULTRASONIC_SENSOR.VCC
  N4: RELAY.COIL1, NPN_TRANSISTOR.1
  N5: RELAY.NO, DC_MOTOR.pin_2
  N6: NPN_TRANSISTOR.0, RESISTOR.Pin_0

custom parts:
  NodeMCU V1.0: ESP8266 based NodeMCU
