# Fritzing sketch bluetooth_intensity_controler_updated (Labelled) (saved by Fritzing 0.9.3b)
breadboards: 1

parts:
  BATTERY_HOLDER = Battery Holders [package=battery_20mm_pth_compact]
  LED = RGB LED (com. anode, rbg) [package="5 mm [THT]"]
  ARDUINO_UNO = Arduino Uno (Rev3) - ICSP
  BLUETOOTH_MODULE_(HC-05) = Bluetooth HC-05 Macho

nets:
  N1: BATTERY_HOLDER.+, ARDUINO_UNO.VIN
  GND: BATTERY_HOLDER.-, LED.common_anode, ARDUINO_UNO.GND, BLUETOOTH_MODULE_(HC-05).GND
  N2: LED.red_cathode, ARDUINO_UNO.D8
  N3: LED.blue_cathode, ARDUINO_UNO.D9_PWM
  N4: LED.green_cathode, ARDUINO_UNO.D10_PWM/SS
  N5: ARDUINO_UNO.D0/RX, BLUETOOTH_MODULE_(HC-05).TXD
  N6: ARDUINO_UNO.D1/TX, BLUETOOTH_MODULE_(HC-05).RXD
  5V: ARDUINO_UNO.5V, BLUETOOTH_MODULE_(HC-05).VCC
