# Fritzing sketch Alcohol Detection (Labelled) (saved by Fritzing 0.9.3b)
breadboards: 1

parts:
  ARDUINO_UNO = Arduino Uno (Rev3)
  ALCOHOL_(MQ3)_SENSOR = GAS_SENSOR [package=mq-3]
  LCD_DISPLAY = LCD screen
  BUZZER = Piezo Speaker
  RESISTOR = Resistor [tolerance=±5% resistance=220 package=THT]  # not connected
  SWITCH = SWITCH-SPST-2 [package=switch-spst-vertical]
  BATTERY = Battery block 9V

nets:
  N1: ARDUINO_UNO.A0, ALCOHOL_(MQ3)_SENSOR.B1
  N2: ARDUINO_UNO.D8, LCD_DISPLAY.DB4
  N3: ARDUINO_UNO.D9_PWM, LCD_DISPLAY.DB7
  N4: ARDUINO_UNO.D12/MISO, LCD_DISPLAY.DB6
  N5: ARDUINO_UNO.D2, BUZZER.pin2
  N6: ARDUINO_UNO.D4, LCD_DISPLAY.DB0
  N7: ARDUINO_UNO.D5_PWM, LCD_DISPLAY.DB1
  N8: ARDUINO_UNO.D6_PWM, LCD_DISPLAY.DB2
  N9: ARDUINO_UNO.D7, LCD_DISPLAY.DB3
  5V: ARDUINO_UNO.5V, LCD_DISPLAY.VDD, LCD_DISPLAY.LED+
  GND: ARDUINO_UNO.GND, LCD_DISPLAY.VSS, LCD_DISPLAY.DB5, LCD_DISPLAY.LED-, BATTERY.-
  N10: ARDUINO_UNO.VIN, SWITCH.O
  N11: ALCOHOL_(MQ3)_SENSOR.A1, ALCOHOL_(MQ3)_SENSOR.H1
  N12: ALCOHOL_(MQ3)_SENSOR.H2, BUZZER.pin1
  N13: SWITCH.P, BATTERY.+
