# Fritzing sketch Smart Distance Meter (Labelled) (saved by Fritzing 0.9.3b)
breadboards: 1

parts:
  ULTRASONIC_SENSOR = HC-SR04 Ultrasonic Distance Sensor
  ARDUINO_UNO = Arduino Uno (Rev3) - ICSP
  LCD_DISPLAY = LCD screen
  POTENTIOMETER = TRIMPOT [package=trim_pot_pth]
  BATTERY_HOLDER = Battery Holders [package=battcon_12mm_pth]

nets:
  VCC: ULTRASONIC_SENSOR.VCC, ARDUINO_UNO.5V, LCD_DISPLAY.VDD, LCD_DISPLAY.LED+, POTENTIOMETER.CW
  N1: ULTRASONIC_SENSOR.TRIG, ARDUINO_UNO.D2
  N2: ULTRASONIC_SENSOR.ECHO, ARDUINO_UNO.D4
  GND: ULTRASONIC_SENSOR.GND, ARDUINO_UNO.GND, LCD_DISPLAY.VSS, LCD_DISPLAY.V0, LCD_DISPLAY.R/W, LCD_DISPLAY.LED-, POTENTIOMETER.CCW, BATTERY_HOLDER.+
  N3: ARDUINO_UNO.A0, POTENTIOMETER.WIPER
  N4: ARDUINO_UNO.D8, LCD_DISPLAY.DB5
  N5: ARDUINO_UNO.D9_PWM, LCD_DISPLAY.DB6
  N6: ARDUINO_UNO.D10_PWM/SS, LCD_DISPLAY.DB7
  N7: ARDUINO_UNO.D5_PWM, LCD_DISPLAY.RS
  N8: ARDUINO_UNO.D6_PWM, LCD_DISPLAY.E
  N9: ARDUINO_UNO.D7, LCD_DISPLAY.DB4
  N10: ARDUINO_UNO.VIN, BATTERY_HOLDER.-
