# Fritzing sketch Smart Dustbin (saved by Fritzing 0.9.3b)
breadboards: 1

parts:
  IC1 = L293D [package=THT]
  Part1 = Arduino Uno (Rev3) - ICSP
  Part2 = HC-SR04 Ultrasonic Rangemeter
  M1 = DC Motor
  Part3 = LilyPad Coin Cell Battery Holder

nets:
  N1: IC1.In_3, Part1.D5_PWM
  N2: IC1.Out_3_(_Controlled_by_Enable_2_), M1.pin_2
  N3: IC1.Out_4_(_Controlled_by_Enable_2_), M1.pin_1
  N4: IC1.In_4, Part1.D6_PWM
  5V: IC1.+V, Part1.5V, Part2.VCC
  N5: Part1.ICSP_MISO, Part1.D12/MISO, Part2.Echo
  GND: Part1.GND, Part1.VIN, Part2.GND, Part3.+
  N6: Part1.D11_PWM/MOSI, Part2.Trig
