# Fritzing sketch Motion_Counter (saved by Fritzing 0.9.3b)
breadboards: 1

parts:
  IR_SENSOR_1 = TSOP312.., 314.. [package=THT]
  BATTERY_HOLDER = Battery Holders [package=battery_20mm_pth_compact]
  ARDUINO = Arduino Uno (Rev3) - ICSP
  IR_SENSOR_2 = TSOP312.., 314.. [package=THT]
  LCD = LCD screen
  BUZZER = Piezo Speaker

nets:
  GND: IR_SENSOR_1.GND, BATTERY_HOLDER.-, IR_SENSOR_2.GND, LCD.LED-, BUZZER.pin1
  N1: IR_SENSOR_1.Vs, BATTERY_HOLDER.+, IR_SENSOR_2.Vs, LCD.LED+
  N2: IR_SENSOR_1.Data, ARDUINO.D10_PWM/SS
  N3: ARDUINO.D8, BUZZER.pin2
  N4: ARDUINO.D11_PWM/MOSI, IR_SENSOR_2.Data
  N5: ARDUINO.D12/MISO, LCD.E
  N6: ARDUINO.D13/SCK, LCD.RS
  N7: ARDUINO.D4, LCD.DB7
  N8: ARDUINO.D5_PWM, LCD.DB6
  N9: ARDUINO.D6_PWM, LCD.DB5
  N10: ARDUINO.D7, LCD.DB4
