# Fritzing sketch robotic_arm_updated (Labelled) (saved by Fritzing 0.9.3b)
breadboards: 1

parts:
  SERVO_MOTOR_2 = Basic Servo
  SERVO_MOTOR_1 = Basic Servo
  SERVO_MOTOR_4 = Basic Servo
  SERVO_MOTOR_3 = Basic Servo
  BATTERY = Battery
  DC-DC_BUCK_CONVERTER_POWER_SUPPLY_MODULE = RioRand LM2596
  JOYSTICK_1 = JOYSTICK-PSP1000 [package=joystick-psp1000]
  JOYSTICK_2 = JOYSTICK-PSP1000 [package=joystick-psp1000]
  ARDUINO_UNO = Arduino Uno (Rev3)

nets:
  GND: SERVO_MOTOR_2.gnd, SERVO_MOTOR_1.gnd, SERVO_MOTOR_4.gnd, SERVO_MOTOR_3.gnd, DC-DC_BUCK_CONVERTER_POWER_SUPPLY_MODULE.Pin_4, JOYSTICK_1.GND, JOYSTICK_2.GND, ARDUINO_UNO.GND
  VCC: SERVO_MOTOR_2.vcc, SERVO_MOTOR_1.vcc, SERVO_MOTOR_4.vcc, SERVO_MOTOR_3.vcc, DC-DC_BUCK_CONVERTER_POWER_SUPPLY_MODULE.Pin_3, JOYSTICK_1.VCC, JOYSTICK_2.VCC, ARDUINO_UNO.VIN
  N1: SERVO_MOTOR_2.pulse, ARDUINO_UNO.D6_PWM
  N2: SERVO_MOTOR_1.pulse, ARDUINO_UNO.D9_PWM
  N3: SERVO_MOTOR_4.pulse, ARDUINO_UNO.D3_PWM
  N4: SERVO_MOTOR_3.pulse, ARDUINO_UNO.D5_PWM
  N5: BATTERY.-, DC-DC_BUCK_CONVERTER_POWER_SUPPLY_MODULE.Pin_1
  N6: BATTERY.+, DC-DC_BUCK_CONVERTER_POWER_SUPPLY_MODULE.Pin_2
  N7: JOYSTICK_1.X, ARDUINO_UNO.A1
  N8: JOYSTICK_1.Y, ARDUINO_UNO.A0
  N9: JOYSTICK_2.X, ARDUINO_UNO.A3
  N10: JOYSTICK_2.Y, ARDUINO_UNO.A2
