# Fritzing sketch robotic_arm_updated (saved by Fritzing 0.9.3b)
breadboards: 1

parts:
  J1 = Basic Servo
  J2 = Basic Servo
  J3 = Basic Servo
  J4 = Basic Servo
  VCC1 = Battery
  M1 = RioRand LM2596
  U1 = JOYSTICK-PSP1000 [package=joystick-psp1000]
  U2 = JOYSTICK-PSP1000 [package=joystick-psp1000]
  Part1 = Arduino Uno (Rev3)

nets:
  GND: J1.gnd, J2.gnd, J3.gnd, J4.gnd, M1.Pin_4, U1.GND, U2.GND, Part1.GND
  VCC: J1.vcc, J2.vcc, J3.vcc, J4.vcc, M1.Pin_3, U1.VCC, U2.VCC, Part1.VIN
  N1: J1.pulse, Part1.D6_PWM
  N2: J2.pulse, Part1.D9_PWM
  N3: J3.pulse, Part1.D3_PWM
  N4: J4.pulse, Part1.D5_PWM
  N5: VCC1.-, M1.Pin_1
  N6: VCC1.+, M1.Pin_2
  N7: U1.X, Part1.A1
  N8: U1.Y, Part1.A0
  N9: U2.X, Part1.A3
  N10: U2.Y, Part1.A2
