# Fritzing sketch Simple weather stationfn (Labelled) (saved by Fritzing 0.9.3b)
circuit board: 8.46667cm x 5.64444cm
breadboards: 1

parts:
  RESISTOR_2 = 220 Ω Resistor [package="0402 [SMD]"]
  PHOTO_RESISTOR = Photocell (LDR) [package=THT]
  BATTERY = Battery block 9V
  RESISTOR = Resistor [tolerance=±5% resistance=4.7k package="0603 [SMD]"]
  TEMPERATURE_HUMIDITY_SENSOR = DHT11 Humitidy and Temperature Sensor
  NODE_MCU = NodeMCU V1.0
  BAROMETRIC_PRESSURE_SENSOR = Barometric Pressure Sensor - BMP180 Breakout (GY-68)

nets:
  GND: RESISTOR_2.Pin_0, BATTERY.-, TEMPERATURE_HUMIDITY_SENSOR.GND, NODE_MCU.GND, BAROMETRIC_PRESSURE_SENSOR.GND
  N1: RESISTOR_2.Pin_1, PHOTO_RESISTOR.pin_0
  N2: PHOTO_RESISTOR.pin_1, NODE_MCU.A0
  N3: BATTERY.+, NODE_MCU.Vin
  VDD: RESISTOR.Pin_0, TEMPERATURE_HUMIDITY_SENSOR.VDD, NODE_MCU.3V3, BAROMETRIC_PRESSURE_SENSOR.VCC
  N4: RESISTOR.Pin_1, TEMPERATURE_HUMIDITY_SENSOR.DATA, NODE_MCU.D4
  N5: NODE_MCU.D1, BAROMETRIC_PRESSURE_SENSOR.SDA
  N6: NODE_MCU.D2, BAROMETRIC_PRESSURE_SENSOR.SCL

custom parts:
  220 Ω Resistor: Resistor Basic schematic elements and footprints for 0603, 1206, and PTH resistors.
  DHT11 Humitidy and Temperature Sensor: DHT11 Humidity and Temperature Sensor
  NodeMCU V1.0: ESP8266 based NodeMCU
