# Fritzing sketch obsticles_update (Labelled) (saved by Fritzing 0.9.3b)
circuit board: 8.46667cm x 5.64444cm
breadboards: 1

parts:
  ARDUINO_UNO = Arduino Uno (Rev3)
  DC_MOTOR_1 = DC Motor
  DC_MOTOR_2 = DC Motor
  BATTERY = Battery
  MOTOR_DRIVER = H-Bridge with L298N
  ULTRASONIC_SENSOR = HC-SR04 Ultrasonic Distance Sensor
  SERVO_MOTOR = Dagu DGServo 9g (Top view) [part_number=RS001B]

nets:
  N1: ARDUINO_UNO.A1, ULTRASONIC_SENSOR.ECHO
  N2: ARDUINO_UNO.A2, ULTRASONIC_SENSOR.TRIG
  N3: ARDUINO_UNO.D9_PWM, SERVO_MOTOR.pulse
  N4: ARDUINO_UNO.D2, MOTOR_DRIVER.IN1
  N5: ARDUINO_UNO.D3_PWM, MOTOR_DRIVER.IN2
  N6: ARDUINO_UNO.D4, MOTOR_DRIVER.IN3
  N7: ARDUINO_UNO.D5_PWM, MOTOR_DRIVER.IN4
  5V: ARDUINO_UNO.5V, MOTOR_DRIVER.5V, ULTRASONIC_SENSOR.VCC, SERVO_MOTOR.vcc
  GND: ARDUINO_UNO.GND, BATTERY.-, MOTOR_DRIVER.GND, ULTRASONIC_SENSOR.GND, SERVO_MOTOR.gnd
  VIN: ARDUINO_UNO.VIN, BATTERY.+, MOTOR_DRIVER.12V
  N8: DC_MOTOR_1.pin_1, MOTOR_DRIVER.M1-02
  N9: DC_MOTOR_1.pin_2, MOTOR_DRIVER.M1-01
  N10: DC_MOTOR_2.pin_1, MOTOR_DRIVER.M2-02
  N11: DC_MOTOR_2.pin_2, MOTOR_DRIVER.M2-01
  N12: MOTOR_DRIVER.ENA, MOTOR_DRIVER.ENA-5V
  N13: MOTOR_DRIVER.ENB, MOTOR_DRIVER.ENB-5V

custom parts:
  H-Bridge with L298N: h-bridge
