# Fritzing sketch Smoke_detector_updated (Labelled) (saved by Fritzing 0.9.3b)
breadboards: 1

parts:
  ARDUINO_UNO = Arduino Uno (Rev3)
  CARBON_MONOXIDE_GAS_SENSOR = MQ-7 breakout
  DC_MOTOR = DC Motor
  LED_1 = smd LED [color="Red (633nm)" package="0805 [SMD]"]
  LED_2 = smd LED [color="Green (570nm)" package="0805 [SMD]"]
  U1 = TRANSISTOR_NPN_2 [package=to-92]
  BATTERY_HOLDER = Battery Holders [package=battery_20mm_pth_compact]
  R1 = Resistor [tolerance=±5% resistance=220 package="2512 [SMD]"]
  BUZZER = Piezo Speaker

nets:
  N1: ARDUINO_UNO.A0, CARBON_MONOXIDE_GAS_SENSOR.AO
  N2: ARDUINO_UNO.D9_PWM, CARBON_MONOXIDE_GAS_SENSOR.DO
  N3: ARDUINO_UNO.D10_PWM/SS, LED_2.anode
  N4: ARDUINO_UNO.D12/MISO, LED_1.anode
  GND: ARDUINO_UNO.GND, CARBON_MONOXIDE_GAS_SENSOR.GND, LED_1.cathode, LED_2.cathode, BATTERY_HOLDER.-, BUZZER.pin1
  N5: ARDUINO_UNO.D2, R1.Pin_1
  N6: ARDUINO_UNO.D3_PWM, BUZZER.pin2
  5V: ARDUINO_UNO.5V, CARBON_MONOXIDE_GAS_SENSOR.VCC
  N7: ARDUINO_UNO.VIN, DC_MOTOR.pin_2, U1.C, BATTERY_HOLDER.+
  N8: DC_MOTOR.pin_1, U1.E
  N9: U1.B, R1.Pin_0

custom parts:
  MQ-7 breakout: SKU: 101282
