# Fritzing sketch fire_fighter_updated (Labelled) (saved by Fritzing 0.9.3b)
circuit board: 8.46667cm x 5.64444cm
breadboards: 1

parts:
  ARDUINO_UNO = Arduino Uno (Rev3)
  DC_MOTOR_1 = DC Motor
  DC_MOTOR_2 = DC Motor
  BATTERY_12V = Battery
  MOTOR_DRIVER_L298N = H-Bridge with L298N
  BUZZER = Piezo Speaker
  FLAME_SENSOR_3 = KY-026
  FLAME_SENSOR_2 = KY-026
  FLAME_SENSOR_1 = KY-026
  SERVO_MOTOR = Dagu DGServo 9g (Top view) [part_number=RS001B]
  DC_MOTOR_3 = DC Motor
  RESISTOR = Resistor [tolerance=±5% resistance=220 package="2512 [SMD]"]
  NPN_TRANSISTOR = NPN-Transistor [package="SOT-23 [SMD]"]

nets (from the breadboard view):
  N1: ARDUINO_UNO.A5/SCL, RESISTOR.Pin_1
  N2: ARDUINO_UNO.D8, FLAME_SENSOR_1.pin4
  N3: ARDUINO_UNO.D9_PWM, FLAME_SENSOR_2.pin4
  N4: ARDUINO_UNO.D10_PWM/SS, FLAME_SENSOR_3.pin4
  N5: ARDUINO_UNO.D11_PWM/MOSI, BUZZER.pin2
  N6: ARDUINO_UNO.D2, MOTOR_DRIVER_L298N.IN1
  N7: ARDUINO_UNO.D3_PWM, MOTOR_DRIVER_L298N.IN2
  N8: ARDUINO_UNO.D4, MOTOR_DRIVER_L298N.IN3
  N9: ARDUINO_UNO.D5_PWM, MOTOR_DRIVER_L298N.IN4
  5V: ARDUINO_UNO.5V, MOTOR_DRIVER_L298N.5V, SERVO_MOTOR.vcc
  GND: ARDUINO_UNO.GND, BATTERY_12V.-, MOTOR_DRIVER_L298N.GND, BUZZER.pin1, FLAME_SENSOR_3.pin2, FLAME_SENSOR_2.pin2, FLAME_SENSOR_1.pin2, DC_MOTOR_3.pin_1
  VIN: ARDUINO_UNO.VIN, BATTERY_12V.+, MOTOR_DRIVER_L298N.12V, FLAME_SENSOR_3.pin3, FLAME_SENSOR_2.pin3, FLAME_SENSOR_1.pin3, NPN_TRANSISTOR.2
  N10: DC_MOTOR_1.pin_1, MOTOR_DRIVER_L298N.M1-02
  N11: DC_MOTOR_1.pin_2, MOTOR_DRIVER_L298N.M1-01
  N12: DC_MOTOR_2.pin_1, MOTOR_DRIVER_L298N.M2-02
  N13: DC_MOTOR_2.pin_2, MOTOR_DRIVER_L298N.M2-01
  N14: MOTOR_DRIVER_L298N.ENA, MOTOR_DRIVER_L298N.ENA-5V
  N15: MOTOR_DRIVER_L298N.ENB, MOTOR_DRIVER_L298N.ENB-5V
  N16: DC_MOTOR_3.pin_2, NPN_TRANSISTOR.1
  N17: RESISTOR.Pin_0, NPN_TRANSISTOR.0

custom parts:
  H-Bridge with L298N: h-bridge
  KY-026: ky-026 flame sensor module
