# Fritzing sketch floor_cleaning_update (Labelled) (saved by Fritzing 0.9.3b)
circuit board: 8.46667cm x 5.64444cm
breadboards: 1

parts:
  ARDUINO_UNO = Arduino Uno (Rev3)
  DC_MOTOR_1 = DC Motor
  DC_MOTOR_2 = DC Motor
  MOTOR_DRIVER = H-Bridge with L298N
  ULTRASONIC_SENSOR = HC-SR04 Ultrasonic Distance Sensor
  9G_SERVO_MOTOR = Dagu DGServo 9g (Top view) [part_number=RS001B]
  NPN_TRANSISTOR = TRANSISTOR_NPN [package=to-92]
  NPN_TRANSISTOR_2 = TRANSISTOR_NPN [package=to-92]
  DC_MOTOR_3 = DC Motor
  DC_MOTOR_4 = DC Motor
  RESISTOR_2 = Resistor [tolerance=±5% resistance=220 package="2512 [SMD]"]
  RESISTOR_1 = Resistor [tolerance=±5% resistance=220 package="2512 [SMD]"]
  BATTERY = Battery Holders [package=battery_20mm_pth_compact]

nets (from the breadboard view):
  N1: ARDUINO_UNO.A1, ULTRASONIC_SENSOR.ECHO
  N2: ARDUINO_UNO.A2, ULTRASONIC_SENSOR.TRIG
  N3: ARDUINO_UNO.D9_PWM, 9G_SERVO_MOTOR.pulse
  GND: ARDUINO_UNO.GND, MOTOR_DRIVER.GND, ULTRASONIC_SENSOR.GND, 9G_SERVO_MOTOR.gnd, DC_MOTOR_3.pin_1, DC_MOTOR_4.pin_1, BATTERY.-
  N4: ARDUINO_UNO.D2, MOTOR_DRIVER.IN1
  N5: ARDUINO_UNO.D3_PWM, MOTOR_DRIVER.IN2
  N6: ARDUINO_UNO.D4, MOTOR_DRIVER.IN3
  N7: ARDUINO_UNO.D5_PWM, MOTOR_DRIVER.IN4
  N8: ARDUINO_UNO.D6_PWM, RESISTOR_1.Pin_0
  N9: ARDUINO_UNO.D7, RESISTOR_2.Pin_0
  VCC: ARDUINO_UNO.5V, ULTRASONIC_SENSOR.VCC, 9G_SERVO_MOTOR.vcc
  VIN: ARDUINO_UNO.VIN, MOTOR_DRIVER.12V, NPN_TRANSISTOR.C, NPN_TRANSISTOR_2.C, BATTERY.+
  N10: DC_MOTOR_1.pin_1, MOTOR_DRIVER.M1-02
  N11: DC_MOTOR_1.pin_2, MOTOR_DRIVER.M1-01
  N12: DC_MOTOR_2.pin_1, MOTOR_DRIVER.M2-02
  N13: DC_MOTOR_2.pin_2, MOTOR_DRIVER.M2-01
  N14: MOTOR_DRIVER.ENA, MOTOR_DRIVER.ENA-5V
  N15: MOTOR_DRIVER.ENB, MOTOR_DRIVER.ENB-5V
  N16: NPN_TRANSISTOR.E, DC_MOTOR_3.pin_2
  N17: NPN_TRANSISTOR.B, RESISTOR_1.Pin_1
  N18: NPN_TRANSISTOR_2.E, DC_MOTOR_4.pin_2
  N19: NPN_TRANSISTOR_2.B, RESISTOR_2.Pin_1

custom parts:
  H-Bridge with L298N: h-bridge
