# Fritzing sketch garage_door_updated (saved by Fritzing 0.9.3b)
breadboards: 1

parts:
  Part1 = Arduino Uno (Rev3) - ICSP
  Part2 = EasyDriver_v44
  Part3 = Bluetooth HC-05 Macho
  M1 = Stepper Motor - Bipolar
  BAT1 = Battery Holders [package=battcon_20mm]  # not connected

nets (from the schematic view):
  5V: Part1.5V, Part3.VCC
  N1: Part1.D8, Part2.DIR
  N2: Part1.D9_PWM, Part2.STEP
  N3: Part1.D0/RX, Part3.TXD
  N4: Part1.D1/TX, Part3.RXD
  N5: Part2.OUT2A, M1.A
  N6: Part2.OUT2B, M1.C
  N7: Part2.OUT1A, M1.B
  N8: Part2.OUT1B, M1.D
